// Logisim project assignment4_CombinationalLogic.circ as structural Verilog
module _1BitAdder (
  input  A,
  input  B,
  input  Ci,
  output S,
  output Co
);

  wire nand_1_out, nand_2_out, nand_3_out, nand_4_out, nand_5_out, nand_6_out, nand_7_out, nand_8_out,
       nand_9_out, nand_10_out, nand_11_out, nand_12_out, nand_13_out;

  nand nand_1 (nand_1_out, A, A);
  nand nand_2 (nand_2_out, B, B);
  nand nand_3 (nand_3_out, A, A);
  nand nand_4 (nand_4_out, Ci, Ci);
  nand nand_5 (nand_5_out, B, B);
  nand nand_6 (nand_6_out, Ci, Ci);
  nand nand_7 (nand_7_out, B, Ci);
  nand nand_8 (nand_8_out, A, Ci);
  nand nand_9 (nand_9_out, A, B);
  nand nand_10 (nand_10_out, nand_1_out, nand_2_out, Ci);
  nand nand_11 (nand_11_out, nand_3_out, B, nand_4_out);
  nand nand_12 (nand_12_out, A, nand_5_out, nand_6_out);
  nand nand_13 (nand_13_out, A, B, Ci);
  nand nand_14 (Co, nand_7_out, nand_8_out, nand_9_out);
  nand nand_15 (S, nand_10_out, nand_11_out, nand_12_out, nand_13_out);
endmodule

module _8BitSubtractor (
  input  in_1,
  input  [7:0] B,
  input  [7:0] A,
  output ZF,
  output CF,
  output [7:0] Result,
  output SF,
  output OF
);

  wire n1bitadder_1_co, n1bitadder_2_co, n1bitadder_3_co, n1bitadder_4_co, n1bitadder_5_co, n1bitadder_6_co,
       n1bitadder_7_co, xor_1_out, xor_2_out, xor_3_out, xor_4_out, xor_5_out, xor_6_out, xor_7_out,
       xor_8_out;

  xor xor_1 (xor_1_out, in_1, B[0]);
  xor xor_2 (xor_2_out, in_1, B[1]);
  xor xor_3 (xor_3_out, in_1, B[2]);
  xor xor_4 (xor_4_out, in_1, B[3]);
  xor xor_5 (xor_5_out, in_1, B[4]);
  xor xor_6 (xor_6_out, in_1, B[5]);
  xor xor_7 (xor_7_out, in_1, B[6]);
  xor xor_8 (xor_8_out, in_1, B[7]);
  _1BitAdder u_1bitadder_1 (.A(in_1), .B(A[0]), .Ci(xor_1_out), .S(Result[0]), .Co(n1bitadder_1_co));
  _1BitAdder u_1bitadder_2 (.A(n1bitadder_1_co), .B(A[1]), .Ci(xor_2_out), .S(Result[1]), .Co(n1bitadder_2_co));
  _1BitAdder u_1bitadder_3 (.A(n1bitadder_2_co), .B(A[2]), .Ci(xor_3_out), .S(Result[2]), .Co(n1bitadder_3_co));
  _1BitAdder u_1bitadder_4 (.A(n1bitadder_3_co), .B(A[3]), .Ci(xor_4_out), .S(Result[3]), .Co(n1bitadder_4_co));
  _1BitAdder u_1bitadder_5 (.A(n1bitadder_4_co), .B(A[4]), .Ci(xor_5_out), .S(Result[4]), .Co(n1bitadder_5_co));
  _1BitAdder u_1bitadder_6 (.A(n1bitadder_5_co), .B(A[5]), .Ci(xor_6_out), .S(Result[5]), .Co(n1bitadder_6_co));
  _1BitAdder u_1bitadder_7 (.A(n1bitadder_6_co), .B(A[6]), .Ci(xor_7_out), .S(Result[6]), .Co(n1bitadder_7_co));
  _1BitAdder u_1bitadder_8 (.A(n1bitadder_7_co), .B(A[7]), .Ci(xor_8_out), .S(Result[7]), .Co(CF));
  NotExactlyOne xnor_1 (
    .out(ZF), .in0(Result[7]), .in1(Result[6]), .in2(Result[5]), .in3(Result[4]), .in4(Result[3]),
    .in5(Result[2]), .in6(Result[1]), .in7(Result[0]));
  xor xor_9 (OF, n1bitadder_7_co, CF);

  assign SF = Result[7];
endmodule

module _8BitAdder (
  input  [7:0] A,
  input  [7:0] B,
  output [7:0] RESULT,
  output CF
);

  wire n1bitadder_1_co, n1bitadder_2_co, n1bitadder_3_co, n1bitadder_4_co, n1bitadder_5_co, n1bitadder_6_co,
       n1bitadder_7_co;

  _1BitAdder u_1bitadder_1 (.A(A[0]), .B(B[0]), .Ci(1'b0), .S(RESULT[0]), .Co(n1bitadder_1_co));
  _1BitAdder u_1bitadder_2 (.A(n1bitadder_1_co), .B(A[1]), .Ci(B[1]), .S(RESULT[1]), .Co(n1bitadder_2_co));
  _1BitAdder u_1bitadder_3 (.A(n1bitadder_2_co), .B(A[2]), .Ci(B[2]), .S(RESULT[2]), .Co(n1bitadder_3_co));
  _1BitAdder u_1bitadder_4 (.A(n1bitadder_3_co), .B(A[3]), .Ci(B[3]), .S(RESULT[3]), .Co(n1bitadder_4_co));
  _1BitAdder u_1bitadder_5 (.A(n1bitadder_4_co), .B(A[4]), .Ci(B[4]), .S(RESULT[4]), .Co(n1bitadder_5_co));
  _1BitAdder u_1bitadder_6 (.A(n1bitadder_5_co), .B(A[5]), .Ci(B[5]), .S(RESULT[5]), .Co(n1bitadder_6_co));
  _1BitAdder u_1bitadder_7 (.A(n1bitadder_6_co), .B(A[6]), .Ci(B[6]), .S(RESULT[6]), .Co(n1bitadder_7_co));
  _1BitAdder u_1bitadder_8 (.A(n1bitadder_7_co), .B(A[7]), .Ci(B[7]), .S(RESULT[7]), .Co(CF));
endmodule
