// Logisim project assignment5_SequentialLogic.circ as structural Verilog
module _1 (
  input  in_1,
  output S0,
  output S1,
  output S2
);

  wire and_1_out, and_2_out, and_3_out, and_4_out, and_5_out, and_6_out, clock_1_out, not_1_out, not_2_out,
       not_3_out, not_4_out, not_5_out, or_1_out, or_2_out, or_3_out;

  not not_1 (not_1_out, S2);
  not not_2 (not_2_out, S0);
  not not_3 (not_3_out, S2);
  not not_4 (not_4_out, S0);
  not not_5 (not_5_out, S1);
  and and_1 (and_1_out, S1, not_1_out);
  or or_1 (or_1_out, and_1_out, and_2_out);
  and and_2 (and_2_out, S0, S2);
  and and_3 (and_3_out, not_2_out, S2);
  or or_2 (or_2_out, and_3_out, and_4_out);
  and and_4 (and_4_out, S1, not_3_out);
  and and_5 (and_5_out, not_4_out, not_5_out);
  or or_3 (or_3_out, and_5_out, and_6_out);
  and and_6 (and_6_out, S0, S1);
  Clock clock_1 (.out(clock_1_out));
  D_Flip_Flop d_ff_1 (.clk(clock_1_out), .D(or_1_out), .Q(S0), .reset(in_1));  // open: Qn, preset, en
  D_Flip_Flop d_ff_2 (.clk(clock_1_out), .D(or_2_out), .Q(S1), .reset(in_1));  // open: Qn, preset, en
  D_Flip_Flop d_ff_3 (.clk(clock_1_out), .D(or_3_out), .Q(S2), .reset(in_1));  // open: Qn, preset, en
endmodule

module _2 (
  input  CLR,
  output Q0,
  output Q5,
  output Q2,
  output Q7,
  output Q4,
  output Q1,
  output Q6,
  output Q3
);

  wire CLK_out, FFA_q, FFA_qn, FFB_q, FFB_qn, FFC_q, FFC_qn, FFD_q, FFD_qn, not_1_out, not_2_out, not_3_out,
       not_4_out, not_5_out, not_6_out, not_7_out, not_8_out, not_9_out, not_10_out, not_11_out, not_12_out,
       not_13_out, not_14_out, not_15_out, not_16_out, not_17_out, not_18_out, not_19_out, not_20_out,
       not_21_out, not_22_out, not_23_out, not_24_out;

  Clock CLK (.out(CLK_out));
  and and_1 (Q0, not_1_out, not_2_out);
  not not_1 (not_1_out, FFD_q);
  not not_2 (not_2_out, FFA_q);
  D_Flip_Flop FFA (.clk(CLK_out), .D(not_21_out), .Q(FFA_q), .Qn(FFA_qn), .reset(not_3_out));  // open: preset, en
  not not_3 (not_3_out, CLR);
  not not_4 (not_4_out, FFA_qn);
  not not_5 (not_5_out, not_4_out);
  not not_6 (not_6_out, not_21_out);
  and and_2 (Q4, not_6_out, not_5_out);
  and and_3 (Q5, not_7_out, not_8_out);
  not not_7 (not_7_out, FFA_q);
  not not_8 (not_8_out, not_9_out);
  not not_9 (not_9_out, FFB_qn);
  D_Flip_Flop FFB (.clk(CLK_out), .D(FFA_q), .Q(FFB_q), .Qn(FFB_qn), .reset(not_10_out));  // open: preset, en
  not not_10 (not_10_out, CLR);
  not not_11 (not_11_out, not_4_out);
  not not_12 (not_12_out, FFB_q);
  and and_4 (Q1, not_11_out, not_12_out);
  and and_5 (Q2, not_14_out, not_13_out);
  not not_13 (not_13_out, FFC_q);
  not not_14 (not_14_out, not_9_out);
  D_Flip_Flop FFC (.clk(CLK_out), .D(FFB_q), .Q(FFC_q), .Qn(FFC_qn), .reset(not_15_out));  // open: preset, en
  not not_15 (not_15_out, CLR);
  not not_16 (not_16_out, FFC_qn);
  not not_17 (not_17_out, FFB_q);
  not not_18 (not_18_out, not_16_out);
  and and_6 (Q6, not_17_out, not_18_out);
  and and_7 (Q7, not_19_out, not_20_out);
  not not_19 (not_19_out, FFC_q);
  not not_20 (not_20_out, not_21_out);
  not not_21 (not_21_out, FFD_qn);
  D_Flip_Flop FFD (.clk(CLK_out), .D(FFC_q), .Q(FFD_q), .Qn(FFD_qn), .reset(not_22_out));  // open: preset, en
  not not_22 (not_22_out, CLR);
  not not_23 (not_23_out, not_16_out);
  not not_24 (not_24_out, FFD_q);
  and and_8 (Q3, not_23_out, not_24_out);
endmodule
